// Logisim project ALU.circ as structural Verilog
module ByPass (
  input  [15:0] PC,
  input  [31:0] MEM_AluResult,
  input  [31:0] WB_AluResult,
  input  [31:0] MEM_Data,
  input  [2:0] RedirectA,
  input  [31:0] RegA,
  input  [2:0] RedirectB,
  input  [31:0] RegB,
  output [31:0] A,
  output [31:0] B
);

  wire [31:0] bit_extender_1_out;

  assign bit_extender_1_out = {{16{1'b0}}, PC};  // Bit_Extender bit_extender_1
  Multiplexer #(.select(3), .width(32), .enable("false")) multiplexer_1 (
    .in0(RegA), .in1(bit_extender_1_out), .in2(MEM_AluResult), .in3(WB_AluResult), .in4(MEM_Data), .out(A),
    .sel(RedirectA));  // open: in5, in6, in7
  Multiplexer #(.select(3), .width(32), .enable("false")) multiplexer_2 (
    .in0(RegB), .in1(bit_extender_1_out), .in2(MEM_AluResult), .in3(WB_AluResult), .in4(MEM_Data), .out(B),
    .sel(RedirectB));  // open: in5, in6, in7
endmodule

module Add32bit (
  input  [31:0] in_1,
  input  [31:0] in_2,
  output [31:0] out_3,
  output OF,
  output CF
);

  wire adder_1_cout;

  Adder #(.width(31)) adder_1 (.a(in_1[30:0]), .b(in_2[30:0]), .out(out_3[30:0]), .cout(adder_1_cout));  // open: cin
  Adder #(.width(1)) adder_2 (.a(in_1[31]), .b(in_2[31]), .out(out_3[31]), .cin(adder_1_cout), .cout(CF));
  xor xor_1 (OF, adder_1_cout, CF);
endmodule

module Sub32bit (
  input  [31:0] in_1,
  input  [31:0] in_2,
  output [31:0] out_3,
  output OF,
  output CF
);

  wire subtractor_1_bout;

  Subtractor #(.width(31)) subtractor_1 (
    .a(in_1[30:0]), .b(in_2[30:0]), .out(out_3[30:0]), .bout(subtractor_1_bout));  // open: bin
  Subtractor #(.width(1)) subtractor_2 (
    .a(in_1[31]), .b(in_2[31]), .out(out_3[31]), .bin(subtractor_1_bout), .bout(CF));
  xor xor_1 (OF, subtractor_1_bout, CF);
endmodule

module ALU (
  input  [31:0] X,
  input  [31:0] Y,
  input  [4:0] Shamt,
  input  [5:0] ALUOP,
  input  IsImm16,
  output [31:0] R,
  output OP,
  output ZF
);

  wire [31:0] alusimp_1_out_6, shiftunit_1_out_5;

  ShiftUnit shiftunit_1 (.X(X), .Y(Y), .Shamt(Shamt), .out_5(shiftunit_1_out_5), .OP(ALUOP[2:0]));
  ALUSimp alusimp_1 (.X(X), .Y(Y), .out_6(alusimp_1_out_6), .Equal(ZF), .OP(ALUOP[3:0]), .OF(OP), .Isimm(IsImm16));
  Multiplexer #(.width(32), .enable("false")) multiplexer_1 (
    .in0(shiftunit_1_out_5), .in1(alusimp_1_out_6), .out(R), .sel(ALUOP[5]));
endmodule

module ShiftUnit (
  input  [31:0] X,
  input  [31:0] Y,
  input  [4:0] Shamt,
  input  [2:0] OP,
  output [31:0] out_5
);

  wire [31:0] shifter_1_out, shifter_2_out, shifter_3_out, shifter_4_out, shifter_5_out, shifter_6_out;

  Shifter #(.width(32)) shifter_1 (.in(Y), .\dist (Shamt), .out(shifter_1_out));
  Shifter #(.width(32), .shift("lr")) shifter_2 (.in(Y), .\dist (Shamt), .out(shifter_2_out));
  Shifter #(.width(32), .shift("ar")) shifter_3 (.in(Y), .\dist (Shamt), .out(shifter_3_out));
  Shifter #(.width(32)) shifter_4 (.in(Y), .\dist (X[4:0]), .out(shifter_4_out));
  Shifter #(.width(32), .shift("lr")) shifter_5 (.in(Y), .\dist (X[4:0]), .out(shifter_5_out));
  Shifter #(.width(32), .shift("ar")) shifter_6 (.in(Y), .\dist (X[4:0]), .out(shifter_6_out));
  Multiplexer #(.select(3), .width(32), .enable("false")) multiplexer_1 (
    .in0(shifter_1_out), .in2(shifter_2_out), .in3(shifter_3_out), .in4(shifter_4_out), .in5(shifter_5_out),
    .in6(shifter_6_out), .out(out_5), .sel(OP));  // open: in1, in7
endmodule

module ALUSimp (
  input  [31:0] X,
  input  [31:0] Y,
  input  [3:0] OP,
  input  Isimm,
  output OF,
  output [31:0] out_6,
  output Equal
);

  wire comparator_1_lt, comparator_2_lt, not_1_out, PlusCF, PlusOF, SubCF, SubOF;
  wire [31:0] add32bit_1_out_3, and_1_out, bit_extender_2_out, bit_extender_3_out, multiplexer_1_out,
       nor_1_out, or_1_out, sub32bit_1_out_3, UY, xor_1_out;

  not not_1 (not_1_out, Isimm);
  Multiplexer #(.width(32), .enable("false")) multiplexer_1 (
    .in0(UY), .in1(Y), .out(multiplexer_1_out), .sel(not_1_out));
  Add32bit add32bit_1 (.in_1(X), .in_2(Y), .out_3(add32bit_1_out_3), .OF(PlusOF), .CF(PlusCF));
  Sub32bit sub32bit_1 (.in_1(X), .in_2(Y), .out_3(sub32bit_1_out_3), .OF(SubOF), .CF(SubCF));
  assign and_1_out = X & multiplexer_1_out;  // AND_Gate and_1, 32 bits wide
  assign or_1_out = X | multiplexer_1_out;  // OR_Gate or_1, 32 bits wide
  assign UY = {{16{1'b0}}, Y[15:0]};  // Bit_Extender bit_extender_1
  assign xor_1_out = X ^ multiplexer_1_out;  // XOR_Gate xor_1, 32 bits wide
  assign nor_1_out = ~(X | multiplexer_1_out);  // NOR_Gate nor_1, 32 bits wide
  Comparator #(.width(32)) comparator_1 (.a(X), .b(Y), .lt(comparator_1_lt));  // open: gt, eq
  assign bit_extender_2_out = {{31{1'b0}}, comparator_1_lt};  // Bit_Extender bit_extender_2
  Comparator #(.width(32), .mode("unsigned")) comparator_2 (
    .a(X), .b(multiplexer_1_out), .eq(Equal), .lt(comparator_2_lt));  // open: gt
  assign bit_extender_3_out = {{31{1'b0}}, comparator_2_lt};  // Bit_Extender bit_extender_3
  Multiplexer #(.select(4), .width(32), .enable("false")) multiplexer_2 (
    .in0(add32bit_1_out_3), .in1(add32bit_1_out_3), .in2(sub32bit_1_out_3), .in3(sub32bit_1_out_3),
    .in4(and_1_out), .in5(or_1_out), .in6(xor_1_out), .in7(nor_1_out), .in10(bit_extender_2_out),
    .in11(bit_extender_3_out), .out(out_6), .sel(OP));  // open: in8, in9, in12, in13, in14, in15
  Multiplexer #(.select(4), .enable("false")) multiplexer_3 (
    .in0(PlusOF), .in1(PlusCF), .in2(SubOF), .in3(SubCF), .in4(1'b0), .in5(1'b0), .in6(1'b0), .in7(1'b0),
    .in8(1'b0), .in9(1'b0), .in10(1'b0), .in11(1'b0), .in12(1'b0), .in13(1'b0), .in14(1'b0), .in15(1'b0),
    .out(OF), .sel(OP));
endmodule
