// Logisim project CPU.circ as structural Verilog
module CPU (
);

  wire alu_1_zf, Block, blocker_1_iee, blocker_1_pce, Branch, Clear, Clock, clock_1_out, control_1_alusrc,
       control_1_memwrite, control_1_out_5, control_1_regwrite, control_1_rsused, control_1_rtused,
       ex_mem_1_memwrite_2, ex_mem_1_regwrite_2, ex_mem_1_syscall_2, id_ex_1_alusrc_2, id_ex_1_memwrite_2,
       id_ex_1_regwrite_2, id_ex_1_syscall_2, insertNopAtEX, instructionsplitter_1_nop, mem_wb_1_regwrite_2,
       mem_wb_1_syscall_2, not_1_out, not_2_out, not_3_out, not_4_out, Print, Reset_out, Stop, unblock;
  wire [1:0] control_1_memmode, control_1_memtoreg, control_1_regdst, id_ex_1_memmode_2, mem_wb_1_memtoreg_2,
       W1Type, W2Type;
  wire [2:0] control_1_jmpop, corrlcheck_1_apd, corrlcheck_1_bpd, id_ex_1_jmpop_2, id_ex_1_sa_2, id_ex_1_sb_2;
  wire [4:0] ex_mem_1_regad_2, id_ex_1_regad_2, id_ex_1_shamt_2, instructionsplitter_1_rd,
       instructionsplitter_1_rs, instructionsplitter_1_rt, instructionsplitter_1_shamt, mem_wb_1_regad_2,
       multiplexer_2_out, W1, W2;
  wire [5:0] control_1_aluop, id_ex_1_aluop_2, instructionsplitter_1_funct, instructionsplitter_1_op;
  wire [6:0] Char;
  wire [15:0] branch_1_to, ex_mem_1_pc_2, id_ex_1_pc_2, if_id_1_out_7, mem_wb_1_pc_2, pcreg_1_out_7,
       pcreg_1_out_8, shifter_1_out, shifter_2_out;
  wire [25:0] id_ex_1_imm_2, instructionsplitter_1_imm26;
  wire [31:0] a0, a1, alu_1_r, bit_extender_1_out, bit_extender_2_out, bypass_1_a, bypass_1_b, ex_mem_1_b_2,
       id_ex_1_a_2, id_ex_1_b_2, if_id_1_out_6, instruction, MA, MD, mips_probe_1_p1, multiplexer_3_out,
       multiplexer_4_out, pipelineview_1_ex, pipelineview_1_id, pipelineview_1_mem, pipelineview_1_wb,
       regsfile_1_rd1, regsfile_1_rd2, v0, WA, \数据存储器_data ;

  Button Reset (.out(Reset_out));
  Blocker blocker_1 (
    .Block(Block), .ID_EX_R(insertNopAtEX), .IIE(unblock), .IEE(blocker_1_iee), .Clock(Clock),
    .Clear(Branch), .PCE(blocker_1_pce));
  Clock clock_1 (.out(clock_1_out));
  PCReg pcreg_1 (
    .Set(Branch), .in_2(branch_1_to), .Clock(not_1_out), .Reset(Reset_out), .out_8(pcreg_1_out_8),
    .out_7(pcreg_1_out_7), .Enable(blocker_1_pce), .Step(16'h4));
  not not_1 (not_1_out, Clock);
  Multiplexer #(.enable("false")) multiplexer_1 (.in0(clock_1_out), .in1(1'b0), .out(Clock), .sel(Stop));
  Shifter #(.width(16), .shift("lr")) shifter_1 (.in(pcreg_1_out_8), .\dist (4'b0010), .out(shifter_1_out));
  IF_ID if_id_1 (
    .IR(instruction), .PC(pcreg_1_out_7), .Clock(Clock), .out_6(if_id_1_out_6), .out_7(if_id_1_out_7),
    .Reset(1'b0), .Enable(unblock));
  ROM #(.addrWidth(16), .dataWidth(32), .Select("low")) \u_指令存储器  (.addr(shifter_1_out), .data(instruction));
  InstructionSplitter instructionsplitter_1 (
    .in_1(if_id_1_out_6), .nop(instructionsplitter_1_nop), .OP(instructionsplitter_1_op),
    .Rs(instructionsplitter_1_rs), .Rt(instructionsplitter_1_rt), .Rd(instructionsplitter_1_rd),
    .Shamt(instructionsplitter_1_shamt), .Funct(instructionsplitter_1_funct),
    .Imm26(instructionsplitter_1_imm26));
  Control control_1 (
    .OP(instructionsplitter_1_op), .Funct(instructionsplitter_1_funct), .MemtoReg(control_1_memtoreg),
    .MemWrite(control_1_memwrite), .JmpOP(control_1_jmpop), .AluOP(control_1_aluop),
    .ALUSrc(control_1_alusrc), .RegWrite(control_1_regwrite), .RegDst(control_1_regdst),
    .MemMode(control_1_memmode), .nop(instructionsplitter_1_nop), .RsUsed(control_1_rsused),
    .RtUsed(control_1_rtused), .out_5(control_1_out_5));
  CorrlCheck corrlcheck_1 (
    .APD(corrlcheck_1_apd), .Conflict(Block), .BPD(corrlcheck_1_bpd), .W1(W1), .W2(W2), .W1Type(W1Type),
    .W2Type(W2Type), .Rs(instructionsplitter_1_rs), .Rt(instructionsplitter_1_rt), .RsUsed(control_1_rsused),
    .RtUsed(control_1_rtused));
  TTY tty_1 (.data(Char), .clk(Clock), .we(Print), .clr(Clear));
  Multiplexer #(.select(2), .width(5), .enable("false")) multiplexer_2 (
    .in0(instructionsplitter_1_rd), .in1(instructionsplitter_1_rt), .in2({5{1'b1}}), .out(multiplexer_2_out),
    .sel(control_1_regdst));  // open: in3
  RegsFile regsfile_1 (
    .Din(multiplexer_4_out), .R1_num(instructionsplitter_1_rs), .R2_num(instructionsplitter_1_rt),
    .Clock(not_2_out), .W_num(mem_wb_1_regad_2), .WE(mem_wb_1_regwrite_2), .RD1(regsfile_1_rd1),
    .RD2(regsfile_1_rd2), .a0(a0), .v0(v0), .a1(a1));
  not not_2 (not_2_out, Clock);
  ID_EX id_ex_1 (
    .MemtoReg(control_1_memtoreg), .MemWrite(control_1_memwrite), .MemMode(control_1_memmode),
    .JmpOP(control_1_jmpop), .AluOP(control_1_aluop), .ALUSrc(control_1_alusrc),
    .RegWrite(control_1_regwrite), .PC(if_id_1_out_7), .A(regsfile_1_rd1), .B(regsfile_1_rd2), .Clock(Clock),
    .MemtoReg_2(W1Type), .MemWrite_2(id_ex_1_memwrite_2), .MemMode_2(id_ex_1_memmode_2),
    .JmpOP_2(id_ex_1_jmpop_2), .AluOP_2(id_ex_1_aluop_2), .ALUSrc_2(id_ex_1_alusrc_2),
    .RegWrite_2(id_ex_1_regwrite_2), .PC_2(id_ex_1_pc_2), .A_2(id_ex_1_a_2), .B_2(id_ex_1_b_2),
    .Imm(instructionsplitter_1_imm26), .Imm_2(id_ex_1_imm_2), .Shamt(instructionsplitter_1_shamt),
    .Shamt_2(id_ex_1_shamt_2), .Reset(insertNopAtEX), .RegAd(multiplexer_2_out), .RegAd_2(id_ex_1_regad_2),
    .Enable(blocker_1_iee), .SA(corrlcheck_1_apd), .SA_2(id_ex_1_sa_2), .SB(corrlcheck_1_bpd),
    .SB_2(id_ex_1_sb_2), .SysCall(control_1_out_5), .SysCall_2(id_ex_1_syscall_2));
  // Mips_Probe mips_probe_1: pin names not known; wires that end beside it: mips_probe_1_p1, instruction
  ByPass bypass_1 (
    .PC(id_ex_1_pc_2), .MEM_AluResult(MA), .WB_AluResult(WA), .MEM_Data(MD), .RegA(id_ex_1_a_2),
    .RegB(id_ex_1_b_2), .A(bypass_1_a), .B(bypass_1_b), .RedirectA(id_ex_1_sa_2), .RedirectB(id_ex_1_sb_2));
  PipelineView pipelineview_1 (
    .in_1(instruction), .Clock(Clock), .InsertNop(insertNopAtEX), .ID(pipelineview_1_id),
    .EX(pipelineview_1_ex), .MEM(pipelineview_1_mem), .WB(pipelineview_1_wb), .IF(mips_probe_1_p1),
    .unblock(unblock));
  assign bit_extender_1_out = {{16{id_ex_1_imm_2[15]}}, id_ex_1_imm_2[15:0]};  // Bit_Extender bit_extender_1
  // Mips_Probe mips_probe_2: pin names not known; wires that end beside it: pipelineview_1_id
  Multiplexer #(.width(32), .enable("false")) multiplexer_3 (
    .in0(bypass_1_b), .in1(bit_extender_1_out), .out(multiplexer_3_out), .sel(id_ex_1_alusrc_2));
  // Mips_Probe mips_probe_3: pin names not known; wires that end beside it: pipelineview_1_ex
  Branch branch_1 (
    .PC_4(id_ex_1_pc_2), .JmpOP(id_ex_1_jmpop_2), .Equal(alu_1_zf), .CMP(alu_1_r), .Imm(id_ex_1_imm_2),
    .RegIn(id_ex_1_a_2), .Jmp(Branch), .To(branch_1_to));
  ALU alu_1 (
    .X(bypass_1_a), .ALUOP(id_ex_1_aluop_2), .Shamt(id_ex_1_shamt_2), .Y(multiplexer_3_out), .ZF(alu_1_zf),
    .R(alu_1_r), .IsImm16(id_ex_1_alusrc_2));  // open: OP
  ExtAnd extand_1 (.X(id_ex_1_regad_2), .Y(id_ex_1_regwrite_2), .Result(W1));
  // Mips_Probe mips_probe_4: pin names not known; wires that end beside it: pipelineview_1_mem
  EX_MEM ex_mem_1 (
    .B(bypass_1_b), .AluResult(alu_1_r), .Clock(Clock), .B_2(ex_mem_1_b_2), .AluResult_2(MA),
    .MemtoReg_2(W2Type), .MemtoReg(W1Type), .MemWrite_2(ex_mem_1_memwrite_2), .MemWrite(id_ex_1_memwrite_2),
    .MemMode(id_ex_1_memmode_2), .RegWrite_2(ex_mem_1_regwrite_2), .RegWrite(id_ex_1_regwrite_2),
    .RegAd(id_ex_1_regad_2), .RegAd_2(ex_mem_1_regad_2), .Reset(1'b0), .Enable(1'b1), .PC(id_ex_1_pc_2),
    .PC_2(ex_mem_1_pc_2), .SysCall(id_ex_1_syscall_2), .SysCall_2(ex_mem_1_syscall_2));  // open: MemMode_2
  Shifter #(.width(16), .shift("lr")) shifter_2 (.in(MA[15:0]), .\dist (4'b0010), .out(shifter_2_out));
  // Mips_Probe mips_probe_5: pin names not known; wires that end beside it: pipelineview_1_wb
  ExtAnd extand_2 (.X(ex_mem_1_regad_2), .Y(ex_mem_1_regwrite_2), .Result(W2));
  RAM #(.addrWidth(16), .dataWidth(32), .bus("separate"), .simpleMode("false"), .Select("low")) \u_数据存储器  (
    .addr(shifter_2_out), .din(ex_mem_1_b_2), .data(\数据存储器_data ), .str(ex_mem_1_memwrite_2), .clk(not_3_out));  // open: sel, ld, clr
  not not_3 (not_3_out, Clock);
  MEM_WB mem_wb_1 (
    .MemtoReg(W2Type), .RegWrite(ex_mem_1_regwrite_2), .MD(\数据存储器_data ), .Clock(Clock),
    .MemtoReg_2(mem_wb_1_memtoreg_2), .RegWrite_2(mem_wb_1_regwrite_2), .MD_2(MD), .AluResult(MA),
    .AluResult_2(WA), .RegAd(ex_mem_1_regad_2), .RegAd_2(mem_wb_1_regad_2), .Reset(1'b0), .Enable(1'b1),
    .PC(ex_mem_1_pc_2), .PC_2(mem_wb_1_pc_2), .SysCall(ex_mem_1_syscall_2), .SysCall_2(mem_wb_1_syscall_2));  // open: MemMode, MemMode_2
  SysCallDecoder syscalldecoder_1 (
    .Clock(not_4_out), .Code(v0), .Enable(mem_wb_1_syscall_2), .Data(a0), .Stop(Stop), .Char(Char),
    .Clear(Clear), .Write(Print));
  not not_4 (not_4_out, Clock);
  assign bit_extender_2_out = {{16{1'b0}}, mem_wb_1_pc_2};  // Bit_Extender bit_extender_2
  Multiplexer #(.select(2), .width(32), .enable("false")) multiplexer_4 (
    .in0(WA), .in1(MD), .in2(bit_extender_2_out), .out(multiplexer_4_out), .sel(mem_wb_1_memtoreg_2));  // open: in3

  // Notes on the sheet:
  //   contents of 指令存储器 (hex, n*v repeats v):
  //   20080000 8d040000 21080004 10800005 2002000b c 42202 1480fffd 1080fff8 2002000a c
endmodule
