// Logisim project Cache.circ as structural Verilog
module main (
);

  Cache cache_1 ();  // open: Block_date, 数据地址, BlkReady, Clock, Dout, Miss
  BlockSwap blockswap_1 ();  // open: Miss, Ready, Dout, Address, out_7, Din, Clock
endmodule

module \Cache直接相联映射  (
  input  [15:0] \数据地址 ,
  input  [31:0] Block_date,
  input  [1:0] Mode,
  input  BlkReady,
  input  [7:0] Din,
  input  Write_enable_on_cache,
  input  Clock,
  input  StoreAll,
  output [7:0] Dout,
  output Write_enable_on_memory,
  output Miss,
  output Store,
  output [31:0] ToStore,
  output StorageComplete,
  output [13:0] AddressForStore
);

  wire and_1_out, and_2_out, and_3_out, and_4_out, comparator_1_eq, not_2_out, \已改写_data , \有效性_data ;
  wire [7:0] controlled_buffer_1_out, counter_1_q, demultiplexer_1_out0, demultiplexer_1_out1,
       demultiplexer_1_out2, demultiplexer_1_out3, multiplexer_2_out;
  wire [31:0] controlled_buffer_2_out;

  Counter counter_1 (
    .Q(counter_1_q), .carry(StorageComplete), .clk(and_1_out));  // open: load, D, count, clr, preset, down
  and and_1 (and_1_out, Clock, StoreAll);
  assign controlled_buffer_1_out = BlkReady ? {\数据地址 [15:10], 2'b10} : 8'bz;  // Controlled_Buffer controlled_buffer_1
  assign controlled_buffer_2_out = BlkReady ? Block_date : 32'bz;  // Controlled_Buffer controlled_buffer_2
  Demultiplexer #(.select(2), .width(8), .enable("false")) demultiplexer_1 (
    .out0(demultiplexer_1_out0), .out1(demultiplexer_1_out1), .out2(demultiplexer_1_out2),
    .out3(demultiplexer_1_out3), .in(Din), .sel(\数据地址 [1:0]));
  assign controlled_buffer_2_out = Write_enable_on_cache ? {demultiplexer_1_out3, demultiplexer_1_out2, demultiplexer_1_out1, demultiplexer_1_out0} : 32'bz;  // Controlled_Buffer controlled_buffer_3
  Multiplexer #(.width(8), .enable("false")) multiplexer_1 (
    .in0(\数据地址 [9:2]), .in1(counter_1_q), .out(AddressForStore[7:0]), .sel(StoreAll));
  RAM #(.dataWidth(1), .bus("separate"), .simpleMode("false"), .Select("low")) \u_已改写  (
    .addr(AddressForStore[7:0]), .din(controlled_buffer_1_out[0]), .data(\已改写_data ), .clk(Clock));  // open: str, sel, ld, clr
  RAM #(.dataWidth(1), .bus("separate"), .simpleMode("false"), .Select("low")) \u_有效性  (
    .addr(AddressForStore[7:0]), .din(controlled_buffer_1_out[1]), .data(\有效性_data ), .clk(Clock));  // open: str, sel, ld, clr
  RAM #(.dataWidth(6), .bus("separate"), .simpleMode("false"), .Select("low")) \u_区地址  (
    .addr(AddressForStore[7:0]), .din(controlled_buffer_1_out[7:2]), .data(AddressForStore[13:8]), .clk(Clock));  // open: str, sel, ld, clr
  Comparator #(.width(6)) comparator_1 (
    .a(AddressForStore[13:8]), .b(\数据地址 [15:10]), .eq(comparator_1_eq));  // open: gt, lt
  and and_2 (and_2_out, comparator_1_eq, \有效性_data );
  and and_3 (and_3_out, Miss, \已改写_data );
  and and_4 (and_4_out, \已改写_data , StoreAll);
  RAM #(.dataWidth(32), .bus("separate"), .simpleMode("false"), .Select("low")) \u_数据块缓冲区  (
    .addr(AddressForStore[7:0]), .din(controlled_buffer_2_out), .data(ToStore), .clk(Clock));  // open: str, sel, ld, clr
  not not_1 (Miss, and_2_out);
  or or_1 (Store, and_3_out, and_4_out);
  Multiplexer #(.select(2), .width(8), .enable("false")) multiplexer_2 (
    .in0(ToStore[7:0]), .in1(ToStore[15:8]), .in2(ToStore[23:16]), .in3(ToStore[31:24]),
    .out(multiplexer_2_out), .sel(\数据地址 [1:0]));
  not not_2 (not_2_out, Miss);
  assign Dout = not_2_out ? multiplexer_2_out : 8'bz;  // Controlled_Buffer controlled_buffer_4

  // Other names for the same wires on the sheet: Tag[5:0] = \数据地址 [15:10]; BlkDataIn[31:0] = Block_date;
  //   WEC = Write_enable_on_cache; WEM = Write_enable_on_memory; offset[1:0] = \数据地址 [1:0]; index[7:0] = \数据地址 [9:2]
endmodule

module Cache (
  input  [31:0] Block_date,
  input  [15:0] \数据地址 ,
  input  BlkReady,
  input  Clock,
  output [7:0] Dout,
  output Miss
);

  wire comparator_1_eq, comparator_2_eq, FistAble, not_1_out, \行译码器_1_地址 ;
  wire [1:1] \有效性_data ;
  wire [7:0] multiplexer_2_out;
  wire [8:0] FistTag;
  wire [17:9] \区地址_data ;
  wire [31:0] Data0, multiplexer_1_out, \数据缓冲区B_data ;

  Pull_Resistor pull_resistor_1 (.node(\数据地址 ));
  RAM #(.addrWidth(5), .dataWidth(2), .bus("separate"), .simpleMode("false"), .Select("low")) \u_有效性  (
    .addr(\数据地址 [6:2]), .din({FistAble, 1'b1}), .data({\有效性_data [1], FistAble}), .str(BlkReady), .clk(Clock));  // open: sel, ld, clr
  RAM #(.addrWidth(5), .dataWidth(18), .bus("separate"), .simpleMode("false"), .Select("low")) \u_区地址  (
    .addr(\数据地址 [6:2]), .din({FistTag, \数据地址 [15:7]}), .data({\区地址_data , FistTag}), .str(BlkReady),
    .clk(Clock));  // open: sel, ld, clr
  Comparator #(.width(9), .mode("unsigned")) comparator_1 (
    .a(\数据地址 [15:7]), .b(FistTag), .eq(comparator_1_eq));  // open: gt, lt
  Comparator #(.width(9), .mode("unsigned")) comparator_2 (
    .a(\数据地址 [15:7]), .b(\区地址_data ), .eq(comparator_2_eq));  // open: gt, lt
  \行译码器  \u_行译码器_1  (
    .Exist0(FistAble), .HitAt0(comparator_1_eq), .Exist1(\有效性_data [1]), .HitAt1(comparator_2_eq),
    .\地址 (\行译码器_1_地址 ), .Miss(Miss));
  RAM #(.addrWidth(5), .dataWidth(32), .bus("separate"), .simpleMode("false"), .Select("low")) \u_数据缓冲区A  (
    .addr(\数据地址 [6:2]), .din(Block_date), .data(Data0), .str(BlkReady), .clk(Clock));  // open: sel, ld, clr
  Multiplexer #(.width(32), .enable("false")) multiplexer_1 (
    .in0(Data0), .in1(\数据缓冲区B_data ), .out(multiplexer_1_out), .sel(\行译码器_1_地址 ));
  RAM #(.addrWidth(5), .dataWidth(32), .bus("separate"), .simpleMode("false"), .Select("low")) \u_数据缓冲区B  (
    .addr(\数据地址 [6:2]), .din(Data0), .data(\数据缓冲区B_data ), .str(BlkReady), .clk(Clock));  // open: sel, ld, clr
  not not_1 (not_1_out, Miss);
  Multiplexer #(.select(2), .width(8), .enable("false")) multiplexer_2 (
    .in0(multiplexer_1_out[7:0]), .in1(multiplexer_1_out[15:8]), .in2(multiplexer_1_out[23:16]),
    .in3(multiplexer_1_out[31:24]), .out(multiplexer_2_out), .sel(\数据地址 [1:0]));
  assign Dout = not_1_out ? multiplexer_2_out : 8'bz;  // Controlled_Buffer controlled_buffer_1

  // Other names for the same wires on the sheet: Tag[8:0] = \数据地址 [15:7]; BlkDataIn[31:0] = Block_date;
  //   offset[1:0] = \数据地址 [1:0]; index[4:0] = \数据地址 [6:2]
endmodule

module \行译码器  (
  input  Exist0,
  input  HitAt0,
  input  Exist1,
  input  HitAt1,
  output \地址 ,
  output Miss
);

  wire and_2_out;

  and and_1 (\地址 , Exist0, HitAt0);
  and and_2 (and_2_out, Exist1, HitAt1);
  nor nor_1 (Miss, \地址 , and_2_out);
endmodule

module BlockSwap (
  input  Miss,
  input  Clock,
  input  [15:0] Address,
  input  [31:0] Din,
  output Ready,
  output [31:0] Dout,
  output [15:0] out_7
);


  assign out_7 = Address;
endmodule

module IChache (
  input  [31:0] Block_date,
  input  [15:0] \数据地址 ,
  input  BlkReady,
  input  Clock,
  output [31:0] Dout,
  output Miss
);

  wire comparator_1_eq, comparator_2_eq, FistAble, not_1_out, \行译码器_1_地址 ;
  wire [1:1] \有效性_data ;
  wire [8:0] FistTag;
  wire [17:9] \区地址_data ;
  wire [31:0] Data0, multiplexer_1_out, \数据缓冲区B_data ;

  Pull_Resistor pull_resistor_1 (.node(\数据地址 ));
  RAM #(.addrWidth(5), .dataWidth(2), .bus("separate"), .simpleMode("false"), .Select("low")) \u_有效性  (
    .addr(\数据地址 [6:2]), .din({FistAble, 1'b1}), .data({\有效性_data [1], FistAble}), .str(BlkReady), .clk(Clock));  // open: sel, ld, clr
  RAM #(.addrWidth(5), .dataWidth(18), .bus("separate"), .simpleMode("false"), .Select("low")) \u_区地址  (
    .addr(\数据地址 [6:2]), .din({FistTag, \数据地址 [15:7]}), .data({\区地址_data , FistTag}), .str(BlkReady),
    .clk(Clock));  // open: sel, ld, clr
  Comparator #(.width(9), .mode("unsigned")) comparator_1 (
    .a(\数据地址 [15:7]), .b(FistTag), .eq(comparator_1_eq));  // open: gt, lt
  Comparator #(.width(9), .mode("unsigned")) comparator_2 (
    .a(\数据地址 [15:7]), .b(\区地址_data ), .eq(comparator_2_eq));  // open: gt, lt
  \行译码器  \u_行译码器_1  (
    .Exist0(FistAble), .HitAt0(comparator_1_eq), .Exist1(\有效性_data [1]), .HitAt1(comparator_2_eq),
    .\地址 (\行译码器_1_地址 ), .Miss(Miss));
  RAM #(.addrWidth(5), .dataWidth(32), .bus("separate"), .simpleMode("false"), .Select("low")) \u_数据缓冲区A  (
    .addr(\数据地址 [6:2]), .din(Block_date), .data(Data0), .str(BlkReady), .clk(Clock));  // open: sel, ld, clr
  Multiplexer #(.width(32), .enable("false")) multiplexer_1 (
    .in0(Data0), .in1(\数据缓冲区B_data ), .out(multiplexer_1_out), .sel(\行译码器_1_地址 ));
  RAM #(.addrWidth(5), .dataWidth(32), .bus("separate"), .simpleMode("false"), .Select("low")) \u_数据缓冲区B  (
    .addr(\数据地址 [6:2]), .din(Data0), .data(\数据缓冲区B_data ), .str(BlkReady), .clk(Clock));  // open: sel, ld, clr
  not not_1 (not_1_out, Miss);
  assign Dout = not_1_out ? multiplexer_1_out : 32'bz;  // Controlled_Buffer controlled_buffer_1

  // Other names for the same wires on the sheet: Tag[8:0] = \数据地址 [15:7]; BlkDataIn[31:0] = Block_date;
  //   index[4:0] = \数据地址 [6:2]
endmodule
