// Logisim project ControlUnit.circ as structural Verilog
module Control (
  input  nop,
  input  [5:0] Funct,
  input  [5:0] OP,
  output RsUsed,
  output out_5,
  output RtUsed,
  output [1:0] MemtoReg,
  output RegWrite,
  output [1:0] MemMode,
  output MemWrite,
  output ALUSrc,
  output [1:0] RegDst,
  output [2:0] JmpOP,
  output [5:0] AluOP
);

  wire alu, alui, and_1_out, and_9_out, and_10_out, AO, beq, bne, comparator_10_eq, comparator_11_eq,
       comparator_12_eq, comparator_13_eq, comparator_14_eq, COP0, eret, IType, j, jal, jr, LO, lw, mfc0,
       or_1_out, RType, sw;
  wire [1:0] priority_encoder_1_out;
  wire [9:0] controlled_buffer_1_out;

  Comparator #(.width(6)) comparator_1 (.a(OP), .b({6{1'b0}}), .eq(RType));  // open: gt, lt
  Comparator #(.width(6)) comparator_2 (.a(OP), .b(6'b000010), .eq(j));  // open: gt, lt
  Comparator #(.width(6)) comparator_3 (.a(OP), .b(6'b000011), .eq(jal));  // open: gt, lt
  Comparator #(.width(6)) comparator_4 (.a(OP), .b(6'b000100), .eq(beq));  // open: gt, lt
  Comparator #(.width(6)) comparator_5 (.a(OP), .b(6'b000101), .eq(bne));  // open: gt, lt
  Comparator #(.width(3)) comparator_6 (.a(OP[5:3]), .b(3'b001), .eq(alui));  // open: gt, lt
  Comparator #(.width(6)) comparator_7 (.a(OP), .b(6'b100011), .eq(lw));  // open: gt, lt
  Comparator #(.width(6)) comparator_8 (.a(OP), .b(6'b101011), .eq(sw));  // open: gt, lt
  Comparator #(.width(6)) comparator_9 (.a(OP), .b(6'b010000), .eq(COP0));  // open: gt, lt
  Comparator #(.width(6)) comparator_10 (.a(Funct), .b(6'b001000), .eq(comparator_10_eq));  // open: gt, lt
  Comparator #(.width(6)) comparator_11 (.a(Funct), .b(6'b001100), .eq(comparator_11_eq));  // open: gt, lt
  and and_1 (and_1_out, ~Funct[4], Funct[5]);  // AND_Gate
  Comparator #(.width(3)) comparator_12 (.a(Funct[5:3]), .b(3'b000), .eq(comparator_12_eq));  // open: gt, lt
  Comparator #(.width(6)) comparator_13 (.a(Funct), .b(6'b111000), .eq(comparator_13_eq));  // open: gt, lt
  Comparator #(.width(3)) comparator_14 (.a(Funct[5:3]), .b(3'b000), .eq(comparator_14_eq));  // open: gt, lt
  and and_2 (jr, RType, comparator_10_eq);
  and and_3 (out_5, RType, comparator_11_eq);
  and and_4 (AO, RType, and_1_out);
  and and_5 (LO, RType, comparator_12_eq);
  and and_6 (eret, COP0, comparator_13_eq);
  and and_7 (mfc0, COP0, comparator_14_eq);
  or or_1 (or_1_out, AO, LO);
  and and_8 (alu, ~nop, or_1_out);  // AND_Gate
  and and_9 (and_9_out, IType, ~RegWrite);  // AND_Gate
  and and_10 (and_10_out, RType, ~nop);  // AND_Gate
  assign controlled_buffer_1_out = nop ? {10{1'b0}} : 10'bz;  // Controlled_Buffer controlled_buffer_1
  assign controlled_buffer_1_out = alu ? 10'h80 : 10'bz;  // Controlled_Buffer controlled_buffer_2
  assign controlled_buffer_1_out = jr ? {10{1'b0}} : 10'bz;  // Controlled_Buffer controlled_buffer_3
  assign controlled_buffer_1_out = j ? {10{1'b0}} : 10'bz;  // Controlled_Buffer controlled_buffer_4
  assign controlled_buffer_1_out = jal ? 10'h284 : 10'bz;  // Controlled_Buffer controlled_buffer_5
  assign controlled_buffer_1_out = beq ? 10'h1 : 10'bz;  // Controlled_Buffer controlled_buffer_6
  assign controlled_buffer_1_out = bne ? 10'h1 : 10'bz;  // Controlled_Buffer controlled_buffer_7
  assign controlled_buffer_1_out = alui ? 10'h8b : 10'bz;  // Controlled_Buffer controlled_buffer_8
  assign controlled_buffer_1_out = lw ? 10'h18b : 10'bz;  // Controlled_Buffer controlled_buffer_9
  assign controlled_buffer_1_out = sw ? 10'h19 : 10'bz;  // Controlled_Buffer controlled_buffer_10
  or or_2 (RsUsed, IType, and_10_out);
  or or_3 (RtUsed, and_9_out, and_10_out);
  Pull_Resistor pull_resistor_1 (.node(controlled_buffer_1_out));
  CCSplitter ccsplitter_1 (
    .in_1(controlled_buffer_1_out), .MemtoReg(MemtoReg), .MemWrite(MemWrite), .MemMode(MemMode),
    .RegWrite(RegWrite), .ALUSrc(ALUSrc), .IType(IType), .RegDst(RegDst));
  Priority_Encoder #(.select(2)) priority_encoder_1 (
    .in0(1'b1), .in1(alu), .in2(alui), .out(priority_encoder_1_out));  // open: in3, gs, en_out, en_in
  Priority_Encoder priority_encoder_2 (
    .in0(1'b1), .in1(jr), .in2(j), .in3(jal), .in4(beq), .in5(bne), .out(JmpOP));  // open: in6, in7, gs, en_out, en_in
  Multiplexer #(.select(2), .width(6), .enable("false")) multiplexer_1 (
    .in0(6'b100000), .in1(Funct), .in2({3'b100, OP[2:0]}), .out(AluOP), .sel(priority_encoder_1_out));  // open: in3

  // Other names for the same wires on the sheet: aluiOP[2:0] = OP[2:0]; SysCode = out_5
endmodule

module CCSplitter (
  input  [9:0] in_1,
  output [1:0] MemtoReg,
  output RegWrite,
  output [1:0] MemMode,
  output MemWrite,
  output ALUSrc,
  output [1:0] RegDst,
  output IType
);


  assign ALUSrc = in_1[3];
  assign IType = in_1[0];
  assign MemMode = in_1[6:5];
  assign MemtoReg = in_1[9:8];
  assign MemWrite = in_1[4];
  assign RegDst = in_1[2:1];
  assign RegWrite = in_1[7];
endmodule

module Blocker (
  input  Clock,
  input  Block,
  input  Clear,
  output PCE,
  output IIE,
  output IEE,
  output ID_EX_R
);

  wire or_1_out, \延迟清空_q , \延迟锁_q ;

  D_Flip_Flop #(.trigger("falling")) \u_延迟锁  (.clk(Clock), .D(Block), .Q(\延迟锁_q ));  // open: Qn, preset, reset
  D_Flip_Flop #(.trigger("falling")) \u_延迟清空  (.clk(Clock), .D(Clear), .Q(\延迟清空_q ));  // open: Qn, preset, reset
  not not_1 (IEE, \延迟锁_q );
  or or_1 (or_1_out, \延迟锁_q , \延迟清空_q );
  and and_1 (ID_EX_R, or_1_out, Clock);

  assign IIE = IEE;
  assign PCE = IEE;
endmodule

module ExtAnd (
  input  [4:0] X,
  input  Y,
  output [4:0] Result
);

  Multiplexer #(.width(5), .enable("false")) multiplexer_1 (.in0({5{1'b0}}), .in1(X), .out(Result), .sel(Y));
endmodule

module InstructionSplitter (
  input  [31:0] in_1,
  output nop,
  output [5:0] OP,
  output [4:0] Rs,
  output [4:0] Rt,
  output [4:0] Rd,
  output [4:0] Shamt,
  output [5:0] Funct,
  output [25:0] Imm26
);

  Comparator #(.width(32)) comparator_1 (.a(in_1), .b({32{1'b0}}), .eq(nop));  // open: gt, lt

  assign Funct = in_1[5:0];
  assign Imm26 = in_1[25:0];
  assign OP = in_1[31:26];
  assign Rd = in_1[15:11];
  assign Rs = in_1[25:21];
  assign Rt = in_1[20:16];
  assign Shamt = in_1[10:6];

  // Other names for the same wires on the sheet: Imm16[15:0] = in_1[15:0]
endmodule

module Branch (
  input  [15:0] PC_4,
  input  [2:0] JmpOP,
  input  Equal,
  input  [31:0] CMP,
  input  [25:0] Imm,
  input  [31:0] RegIn,
  output Jmp,
  output [15:0] To
);

  wire BEQ, BNE, decoder_1_out1, decoder_1_out2, decoder_1_out3, NoJmp, nor_1_out, or_1_out, or_2_out;
  wire [15:0] adder_1_out, Addr;

  Shifter #(.width(16)) shifter_1 (.in(Imm[15:0]), .\dist (4'b0010), .out(Addr));
  Decoder #(.select(3), .enable("false")) decoder_1 (
    .out0(NoJmp), .out1(decoder_1_out1), .out2(decoder_1_out2), .out3(decoder_1_out3), .out4(BEQ),
    .out5(BNE), .sel(JmpOP));  // open: out6, out7
  assign To = decoder_1_out1 ? RegIn[15:0] : 16'bz;  // Controlled_Buffer controlled_buffer_1
  or or_1 (or_1_out, decoder_1_out2, decoder_1_out3);
  assign To = or_1_out ? Addr : 16'bz;  // Controlled_Buffer controlled_buffer_2
  or or_2 (or_2_out, BEQ, BNE);
  Adder #(.width(16)) adder_1 (.a(PC_4), .b(Addr), .out(adder_1_out));  // open: cin, cout
  assign To = or_2_out ? adder_1_out : 16'bz;  // Controlled_Buffer controlled_buffer_3
  nor nor_1 (nor_1_out, NoJmp, JmpOP[2]);
  assign Jmp = BEQ ? Equal : 1'bz;  // Controlled_Buffer controlled_buffer_4
  assign Jmp = BNE ? ~Equal : 1'bz;  // Controlled_Inverter controlled_inverter_1
  assign Jmp = nor_1_out ? nor_1_out : 1'bz;  // Controlled_Buffer controlled_buffer_5
  Pull_Resistor pull_resistor_1 (.node(Jmp));

  // Other names for the same wires on the sheet: Less = CMP[0]; Conditioned = JmpOP[2]
endmodule

module CorrlCheck (
  input  [4:0] W1,
  input  [4:0] W2,
  input  [1:0] W1Type,
  input  [1:0] W2Type,
  input  [4:0] Rs,
  input  RsUsed,
  input  [4:0] Rt,
  input  RtUsed,
  output [2:0] APD,
  output Conflict,
  output [2:0] BPD
);

  wire dataselect_1_conflict, dataselect_2_conflict;

  DataSelect dataselect_1 (
    .RsUsed(RsUsed), .Rs(Rs), .APass(APD), .Conflict(dataselect_1_conflict), .W1Type(W1Type),
    .W2Type(W2Type), .W1(W1), .W2(W2));
  DataSelect dataselect_2 (
    .RsUsed(RtUsed), .Rs(Rt), .APass(BPD), .Conflict(dataselect_2_conflict), .W1Type(W1Type),
    .W2Type(W2Type), .W1(W1), .W2(W2));
  or or_1 (Conflict, dataselect_1_conflict, dataselect_2_conflict);
endmodule

module DataSelect (
  input  RsUsed,
  input  [4:0] Rs,
  input  [4:0] W1,
  input  [1:0] W1Type,
  input  [4:0] W2,
  input  [1:0] W2Type,
  output Conflict,
  output [2:0] APass
);

  wire and_1_out, and_2_out, and_4_out, comparator_1_eq, comparator_2_eq, comparator_3_eq, nor_1_out,
       or_1_out;
  wire [2:0] multiplexer_1_out, w1s_1_select, w2s_1_select;

  Comparator #(.width(5), .mode("unsigned")) comparator_1 (.a(Rs), .b(W1), .eq(comparator_1_eq));  // open: gt, lt
  W1S w1s_1 (.Select(w1s_1_select), .WType(W1Type));
  Comparator #(.width(5), .mode("unsigned")) comparator_2 (.a(Rs), .b(W2), .eq(comparator_2_eq));  // open: gt, lt
  W2S w2s_1 (.WType(W2Type), .Select(w2s_1_select));
  Comparator #(.width(5), .mode("unsigned")) comparator_3 (
    .a(Rs), .b({5{1'b0}}), .eq(comparator_3_eq));  // open: gt, lt
  and and_1 (and_1_out, ~comparator_3_eq, comparator_1_eq, RsUsed);  // AND_Gate
  and and_2 (and_2_out, ~comparator_3_eq, comparator_2_eq, RsUsed);  // AND_Gate
  nor nor_1 (nor_1_out, w1s_1_select[0], w1s_1_select[1], w1s_1_select[2]);
  and and_3 (Conflict, and_1_out, nor_1_out);
  and and_4 (and_4_out, ~and_1_out, and_2_out);  // AND_Gate
  Multiplexer #(.width(3), .enable("false")) multiplexer_1 (
    .in0(w1s_1_select), .in1(w2s_1_select), .out(multiplexer_1_out), .sel(and_4_out));
  or or_1 (or_1_out, and_1_out, and_2_out);
  assign APass = or_1_out ? multiplexer_1_out : 3'bz;  // Controlled_Buffer controlled_buffer_1
  Pull_Resistor pull_resistor_1 (.node(APass));
endmodule

module W1S (
  input  [1:0] WType,
  output [2:0] Select
);

  nor nor_1 (Select[1], WType[1], WType[0]);

  assign {Select[2], Select[0]} = {1'b0, WType[1]};
endmodule

module W2S (
  input  [1:0] WType,
  output [2:0] Select
);

  not not_1 (Select[0], WType[0]);
  nor nor_1 (Select[1], WType[1], WType[0]);

  assign Select[2] = WType[0];
endmodule
