// Logisim project Debug.circ as structural Verilog
module PipelineView (
  input  [31:0] in_1,
  input  Clock,
  input  InsertNop,
  input  unblock,
  output [31:0] IF,
  output [31:0] ID,
  output [31:0] EX,
  output [31:0] MEM,
  output [31:0] WB
);

  Register #(.width(32), .Select("low")) register_1 (.D(in_1), .en(unblock), .Q(ID), .clk(Clock));  // open: clr
  Register #(.width(32), .Select("low")) register_2 (.D(ID), .en(unblock), .Q(EX), .clk(Clock), .clr(InsertNop));
  Register #(.width(32), .Select("low")) register_3 (.D(EX), .Q(MEM), .clk(Clock));  // open: en, clr
  Register #(.width(32), .Select("low")) register_4 (.D(MEM), .Q(WB), .clk(Clock));  // open: en, clr

  assign IF = in_1;
endmodule
