// Logisim project ExternalCircuitry.circ as structural Verilog
module SysCallDecoder (
  input  Clock,
  input  Enable,
  input  [31:0] Data,
  input  [31:0] Code,
  output Stop,
  output Clear,
  output [6:0] Char,
  output Write
);

  wire clearScreen, printChar, stop_t;
  wire [7:7] datasplitter_1_char;
  wire [31:0] Data_t, multiplexer_2_out, register_3_q;

  Multiplexer #(.width(32), .enable("false")) multiplexer_1 (.in0({32{1'b0}}), .in1(Data), .out(Data_t), .sel(Enable));
  Multiplexer #(.width(32), .enable("false")) multiplexer_2 (
    .in0({32{1'b0}}), .in1(Code), .out(multiplexer_2_out), .sel(Enable));
  Comparator #(.width(32), .mode("unsigned")) comparator_1 (
    .a(multiplexer_2_out), .b(32'ha), .eq(stop_t));  // open: gt, lt
  Comparator #(.width(32), .mode("unsigned")) comparator_2 (
    .a(multiplexer_2_out), .b(32'hb), .eq(printChar));  // open: gt, lt
  Comparator #(.width(32), .mode("unsigned")) comparator_3 (
    .a(multiplexer_2_out), .b(32'h25), .eq(clearScreen));  // open: gt, lt
  Register #(.width(1), .Select("low")) register_1 (.D(stop_t), .Q(Stop), .clk(Clock));  // open: en, clr
  Register #(.width(1), .Select("low")) register_2 (.D(clearScreen), .Q(Clear), .clk(Clock));  // open: en, clr
  Register #(.width(32), .Select("low")) register_3 (.D(Data_t), .Q(register_3_q), .clk(Clock));  // open: en, clr
  Register #(.width(1), .Select("low")) register_4 (.D(printChar), .Q(Write), .clk(Clock));  // open: en, clr
  DataSplitter datasplitter_1 (.Data(register_3_q), .Char({datasplitter_1_char[7], Char}));  // open: OP, Addr, Empty
endmodule

module DataSplitter (
  input  [31:0] Data,
  output [7:0] OP,
  output [7:0] Addr,
  output [7:0] Empty,
  output [7:0] Char
);


  assign Addr = Data[23:16];
  assign Char = Data[7:0];
  assign Empty = Data[15:8];
  assign OP = Data[31:24];
endmodule
