// Logisim project Pipeline.circ as structural Verilog
module IF_ID (
  input  [31:0] IR,
  input  [15:0] PC,
  input  Enable,
  input  Clock,
  input  Reset,
  output [31:0] out_6,
  output [15:0] out_7
);

  Register #(.width(32), .Select("low")) register_1 (.D(IR), .en(Enable), .Q(out_6), .clk(Clock), .clr(Reset));
  Register #(.width(16), .Select("low")) register_2 (.D(PC), .en(Enable), .Q(out_7), .clk(Clock), .clr(Reset));
endmodule

module ID_EX (
  input  SysCall,
  input  [1:0] MemtoReg,
  input  MemWrite,
  input  [1:0] MemMode,
  input  [4:0] RegAd,
  input  RegWrite,
  input  [2:0] JmpOP,
  input  [5:0] AluOP,
  input  ALUSrc,
  input  [2:0] SA,
  input  [2:0] SB,
  input  [15:0] PC,
  input  [31:0] A,
  input  [31:0] B,
  input  [4:0] Shamt,
  input  [25:0] Imm,
  input  Enable,
  input  Clock,
  input  Reset,
  output SysCall_2,
  output [1:0] MemtoReg_2,
  output MemWrite_2,
  output [1:0] MemMode_2,
  output [4:0] RegAd_2,
  output RegWrite_2,
  output [2:0] JmpOP_2,
  output [5:0] AluOP_2,
  output ALUSrc_2,
  output [2:0] SA_2,
  output [2:0] SB_2,
  output [15:0] PC_2,
  output [31:0] A_2,
  output [31:0] B_2,
  output [4:0] Shamt_2,
  output [25:0] Imm_2
);

  Register #(.width(1), .Select("low")) register_1 (.D(SysCall), .en(Enable), .Q(SysCall_2), .clk(Clock), .clr(Reset));
  Register #(.width(2), .Select("low")) register_2 (
    .D(MemtoReg), .en(Enable), .Q(MemtoReg_2), .clk(Clock), .clr(Reset));
  Register #(.width(1), .Select("low")) register_3 (
    .D(MemWrite), .en(Enable), .Q(MemWrite_2), .clk(Clock), .clr(Reset));
  Register #(.width(2), .Select("low")) register_4 (.D(MemMode), .en(Enable), .Q(MemMode_2), .clk(Clock), .clr(Reset));
  Register #(.width(5), .Select("low")) register_5 (.D(RegAd), .en(Enable), .Q(RegAd_2), .clk(Clock), .clr(Reset));
  Register #(.width(1), .Select("low")) register_6 (
    .D(RegWrite), .en(Enable), .Q(RegWrite_2), .clk(Clock), .clr(Reset));
  Register #(.width(3), .Select("low")) register_7 (.D(JmpOP), .en(Enable), .Q(JmpOP_2), .clk(Clock), .clr(Reset));
  Register #(.width(6), .Select("low")) register_8 (.D(AluOP), .en(Enable), .Q(AluOP_2), .clk(Clock), .clr(Reset));
  Register #(.width(1), .Select("low")) register_9 (.D(ALUSrc), .en(Enable), .Q(ALUSrc_2), .clk(Clock), .clr(Reset));
  Register #(.width(3), .Select("low")) register_10 (.D(SA), .en(Enable), .Q(SA_2), .clk(Clock), .clr(Reset));
  Register #(.width(3), .Select("low")) register_11 (.D(SB), .en(Enable), .Q(SB_2), .clk(Clock), .clr(Reset));
  Register #(.width(16), .Select("low")) register_12 (.D(PC), .en(Enable), .Q(PC_2), .clk(Clock), .clr(Reset));
  Register #(.width(32), .Select("low")) register_13 (.D(A), .en(Enable), .Q(A_2), .clk(Clock), .clr(Reset));
  Register #(.width(32), .Select("low")) register_14 (.D(B), .en(Enable), .Q(B_2), .clk(Clock), .clr(Reset));
  Register #(.width(5), .Select("low")) register_15 (.D(Shamt), .en(Enable), .Q(Shamt_2), .clk(Clock), .clr(Reset));
  Register #(.width(26), .Select("low")) register_16 (.D(Imm), .en(Enable), .Q(Imm_2), .clk(Clock), .clr(Reset));
endmodule

module EX_MEM (
  input  SysCall,
  input  [1:0] MemtoReg,
  input  MemWrite,
  input  [1:0] MemMode,
  input  [4:0] RegAd,
  input  RegWrite,
  input  [15:0] PC,
  input  [31:0] B,
  input  [31:0] AluResult,
  input  Enable,
  input  Clock,
  input  Reset,
  output SysCall_2,
  output [1:0] MemtoReg_2,
  output MemWrite_2,
  output [1:0] MemMode_2,
  output [4:0] RegAd_2,
  output RegWrite_2,
  output [15:0] PC_2,
  output [31:0] B_2,
  output [31:0] AluResult_2
);

  Register #(.width(1), .Select("low")) register_1 (.D(SysCall), .en(Enable), .Q(SysCall_2), .clk(Clock), .clr(Reset));
  Register #(.width(2), .Select("low")) register_2 (
    .D(MemtoReg), .en(Enable), .Q(MemtoReg_2), .clk(Clock), .clr(Reset));
  Register #(.width(1), .Select("low")) register_3 (
    .D(MemWrite), .en(Enable), .Q(MemWrite_2), .clk(Clock), .clr(Reset));
  Register #(.width(2), .Select("low")) register_4 (.D(MemMode), .en(Enable), .Q(MemMode_2), .clk(Clock), .clr(Reset));
  Register #(.width(5), .Select("low")) register_5 (.D(RegAd), .en(Enable), .Q(RegAd_2), .clk(Clock), .clr(Reset));
  Register #(.width(1), .Select("low")) register_6 (
    .D(RegWrite), .en(Enable), .Q(RegWrite_2), .clk(Clock), .clr(Reset));
  Register #(.width(16), .Select("low")) register_7 (.D(PC), .en(Enable), .Q(PC_2), .clk(Clock), .clr(Reset));
  Register #(.width(32), .Select("low")) register_8 (.D(B), .en(Enable), .Q(B_2), .clk(Clock), .clr(Reset));
  Register #(.width(32), .Select("low")) register_9 (
    .D(AluResult), .en(Enable), .Q(AluResult_2), .clk(Clock), .clr(Reset));
endmodule

module MEM_WB (
  input  SysCall,
  input  [1:0] MemtoReg,
  input  [1:0] MemMode,
  input  [4:0] RegAd,
  input  RegWrite,
  input  [15:0] PC,
  input  [31:0] MD,
  input  [31:0] AluResult,
  input  Enable,
  input  Clock,
  input  Reset,
  output SysCall_2,
  output [1:0] MemtoReg_2,
  output [1:0] MemMode_2,
  output [4:0] RegAd_2,
  output RegWrite_2,
  output [15:0] PC_2,
  output [31:0] MD_2,
  output [31:0] AluResult_2
);

  Register #(.width(1), .Select("low")) register_1 (.D(SysCall), .en(Enable), .Q(SysCall_2), .clk(Clock), .clr(Reset));
  Register #(.width(2), .Select("low")) register_2 (
    .D(MemtoReg), .en(Enable), .Q(MemtoReg_2), .clk(Clock), .clr(Reset));
  Register #(.width(2), .Select("low")) register_3 (.D(MemMode), .en(Enable), .Q(MemMode_2), .clk(Clock), .clr(Reset));
  Register #(.width(5), .Select("low")) register_4 (.D(RegAd), .en(Enable), .Q(RegAd_2), .clk(Clock), .clr(Reset));
  Register #(.width(1), .Select("low")) register_5 (
    .D(RegWrite), .en(Enable), .Q(RegWrite_2), .clk(Clock), .clr(Reset));
  Register #(.width(16), .Select("low")) register_6 (.D(PC), .en(Enable), .Q(PC_2), .clk(Clock), .clr(Reset));
  Register #(.width(32), .Select("low")) register_7 (.D(MD), .en(Enable), .Q(MD_2), .clk(Clock), .clr(Reset));
  Register #(.width(32), .Select("low")) register_8 (
    .D(AluResult), .en(Enable), .Q(AluResult_2), .clk(Clock), .clr(Reset));
endmodule
