// Logisim project Registers.circ as structural Verilog
module PCReg (
  input  Set,
  input  [15:0] in_2,
  input  [15:0] Step,
  input  Enable,
  input  Clock,
  input  Reset,
  output [15:0] out_7,
  output [15:0] out_8
);

  wire not_1_out;
  wire [15:0] controlled_buffer_1_out;

  not not_1 (not_1_out, Set);
  assign controlled_buffer_1_out = not_1_out ? out_7 : 16'bz;  // Controlled_Buffer controlled_buffer_1
  assign controlled_buffer_1_out = Set ? in_2 : 16'bz;  // Controlled_Buffer controlled_buffer_2
  Register #(.width(16), .Select("low")) register_1 (
    .D(controlled_buffer_1_out), .en(Enable), .Q(out_8), .clk(Clock), .clr(Reset));
  Adder #(.width(16)) adder_1 (.a(out_8), .b(Step), .out(out_7));  // open: cin, cout
endmodule

module _4RegsZero (
  input  [1:0] R1_num,
  input  Clock,
  input  [1:0] R2_num,
  input  WE,
  input  [1:0] W_num,
  input  [31:0] Din,
  output [31:0] Reg2_out,
  output [31:0] Reg1_out
);

  wire and_1_out, demultiplexer_1_out1, demultiplexer_1_out2, demultiplexer_1_out3;
  wire [31:0] register_1_q, register_2_q, register_3_q;

  and and_1 (and_1_out, WE, Clock);
  Demultiplexer #(.select(2), .enable("false")) demultiplexer_1 (
    .out1(demultiplexer_1_out1), .out2(demultiplexer_1_out2), .out3(demultiplexer_1_out3), .in(and_1_out),
    .sel(W_num));  // open: out0
  Multiplexer #(.select(2), .width(32), .enable("false")) multiplexer_1 (
    .in0({32{1'b0}}), .in1(register_1_q), .in2(register_2_q), .in3(register_3_q), .out(Reg2_out), .sel(R2_num));
  Register #(.width(32), .Select("low")) register_1 (
    .D(Din), .Q(register_1_q), .clk(demultiplexer_1_out1));  // open: en, clr
  Register #(.width(32), .Select("low")) register_2 (
    .D(Din), .Q(register_2_q), .clk(demultiplexer_1_out2));  // open: en, clr
  Register #(.width(32), .Select("low")) register_3 (
    .D(Din), .Q(register_3_q), .clk(demultiplexer_1_out3));  // open: en, clr
  Multiplexer #(.select(2), .width(32), .enable("false")) multiplexer_2 (
    .in0({32{1'b0}}), .in1(register_1_q), .in2(register_2_q), .in3(register_3_q), .out(Reg1_out), .sel(R1_num));
endmodule

module _4Regs (
  input  [1:0] R1_num,
  input  Clock,
  input  [1:0] R2_num,
  input  WE,
  input  [1:0] W_num,
  input  [31:0] Din,
  output [31:0] Reg2_out,
  output [31:0] Reg1_out
);

  wire and_1_out, demultiplexer_1_out0, demultiplexer_1_out1, demultiplexer_1_out2, demultiplexer_1_out3;
  wire [31:0] register_1_q, register_2_q, register_3_q, register_4_q;

  and and_1 (and_1_out, WE, Clock);
  Demultiplexer #(.select(2), .enable("false")) demultiplexer_1 (
    .out0(demultiplexer_1_out0), .out1(demultiplexer_1_out1), .out2(demultiplexer_1_out2),
    .out3(demultiplexer_1_out3), .in(and_1_out), .sel(W_num));
  Multiplexer #(.select(2), .width(32), .enable("false")) multiplexer_1 (
    .in0(register_1_q), .in1(register_2_q), .in2(register_3_q), .in3(register_4_q), .out(Reg2_out),
    .sel(R2_num));
  Register #(.width(32), .Select("low")) register_1 (
    .D(Din), .Q(register_1_q), .clk(demultiplexer_1_out0));  // open: en, clr
  Register #(.width(32), .Select("low")) register_2 (
    .D(Din), .Q(register_2_q), .clk(demultiplexer_1_out1));  // open: en, clr
  Register #(.width(32), .Select("low")) register_3 (
    .D(Din), .Q(register_3_q), .clk(demultiplexer_1_out2));  // open: en, clr
  Register #(.width(32), .Select("low")) register_4 (
    .D(Din), .Q(register_4_q), .clk(demultiplexer_1_out3));  // open: en, clr
  Multiplexer #(.select(2), .width(32), .enable("false")) multiplexer_2 (
    .in0(register_1_q), .in1(register_2_q), .in2(register_3_q), .in3(register_4_q), .out(Reg1_out),
    .sel(R1_num));
endmodule

module RegsFileZero16 (
  input  [3:0] R1_num,
  input  [31:0] in_2,
  input  [3:0] R2_num,
  input  [3:0] Write_Reg_num,
  input  Write_Enable,
  input  Clock,
  output [31:0] Reg2_out,
  output [31:0] Reg1_out
);

  wire demultiplexer_1_out0, demultiplexer_1_out1, demultiplexer_1_out2, demultiplexer_1_out3;
  wire [31:0] n4regs_1_reg1_out, n4regs_1_reg2_out, n4regs_2_reg1_out, n4regs_2_reg2_out, n4regs_3_reg1_out,
       n4regs_3_reg2_out, n4regszero_1_reg1_out, n4regszero_1_reg2_out;

  Demultiplexer #(.select(2), .enable("false")) demultiplexer_1 (
    .out0(demultiplexer_1_out0), .out1(demultiplexer_1_out1), .out2(demultiplexer_1_out2),
    .out3(demultiplexer_1_out3), .in(Write_Enable), .sel(Write_Reg_num[3:2]));
  _4RegsZero u_4regszero_1 (
    .R1_num(R1_num[1:0]), .Clock(Clock), .R2_num(R2_num[1:0]), .WE(demultiplexer_1_out0),
    .W_num(Write_Reg_num[1:0]), .Reg2_out(n4regszero_1_reg2_out), .Reg1_out(n4regszero_1_reg1_out), .Din(in_2));
  _4Regs u_4regs_1 (
    .R1_num(R1_num[1:0]), .Clock(Clock), .R2_num(R2_num[1:0]), .Din(in_2), .Reg2_out(n4regs_1_reg2_out),
    .Reg1_out(n4regs_1_reg1_out), .W_num(Write_Reg_num[1:0]), .WE(demultiplexer_1_out1));
  _4Regs u_4regs_2 (
    .R1_num(R1_num[1:0]), .Clock(Clock), .R2_num(R2_num[1:0]), .Din(in_2), .Reg2_out(n4regs_2_reg2_out),
    .Reg1_out(n4regs_2_reg1_out), .W_num(Write_Reg_num[1:0]), .WE(demultiplexer_1_out2));
  _4Regs u_4regs_3 (
    .R1_num(R1_num[1:0]), .Clock(Clock), .R2_num(R2_num[1:0]), .Din(in_2), .Reg2_out(n4regs_3_reg2_out),
    .Reg1_out(n4regs_3_reg1_out), .W_num(Write_Reg_num[1:0]), .WE(demultiplexer_1_out3));
  Multiplexer #(.select(2), .width(32), .enable("false")) multiplexer_1 (
    .in0(n4regszero_1_reg2_out), .in1(n4regs_1_reg2_out), .in2(n4regs_2_reg2_out), .in3(n4regs_3_reg2_out),
    .out(Reg2_out), .sel(R2_num[3:2]));
  Multiplexer #(.select(2), .width(32), .enable("false")) multiplexer_2 (
    .in0(n4regszero_1_reg1_out), .in1(n4regs_1_reg1_out), .in2(n4regs_2_reg1_out), .in3(n4regs_3_reg1_out),
    .out(Reg1_out), .sel(R1_num[3:2]));

  // Other names for the same wires on the sheet: Din[31:0] = in_2; W_num[3:0] = Write_Reg_num; WE = Write_Enable
endmodule

module RegsFile16 (
  input  [3:0] R1_num,
  input  [31:0] in_2,
  input  [3:0] R2_num,
  input  [3:0] Write_Reg_num,
  input  Write_Enable,
  input  Clock,
  output [31:0] Reg2_out,
  output [31:0] Reg1_out
);

  wire demultiplexer_1_out0, demultiplexer_1_out1, demultiplexer_1_out2, demultiplexer_1_out3;
  wire [31:0] n4regs_1_reg1_out, n4regs_1_reg2_out, n4regs_2_reg1_out, n4regs_2_reg2_out, n4regs_3_reg1_out,
       n4regs_3_reg2_out, n4regs_4_reg1_out, n4regs_4_reg2_out;

  Demultiplexer #(.select(2), .enable("false")) demultiplexer_1 (
    .out0(demultiplexer_1_out0), .out1(demultiplexer_1_out1), .out2(demultiplexer_1_out2),
    .out3(demultiplexer_1_out3), .in(Write_Enable), .sel(Write_Reg_num[3:2]));
  _4Regs u_4regs_1 (
    .R1_num(R1_num[1:0]), .Clock(Clock), .R2_num(R2_num[1:0]), .Din(in_2), .Reg2_out(n4regs_1_reg2_out),
    .Reg1_out(n4regs_1_reg1_out), .W_num(Write_Reg_num[1:0]), .WE(demultiplexer_1_out0));
  _4Regs u_4regs_2 (
    .R1_num(R1_num[1:0]), .Clock(Clock), .R2_num(R2_num[1:0]), .Din(in_2), .Reg2_out(n4regs_2_reg2_out),
    .Reg1_out(n4regs_2_reg1_out), .W_num(Write_Reg_num[1:0]), .WE(demultiplexer_1_out1));
  _4Regs u_4regs_3 (
    .R1_num(R1_num[1:0]), .Clock(Clock), .R2_num(R2_num[1:0]), .Din(in_2), .Reg2_out(n4regs_3_reg2_out),
    .Reg1_out(n4regs_3_reg1_out), .W_num(Write_Reg_num[1:0]), .WE(demultiplexer_1_out2));
  _4Regs u_4regs_4 (
    .R1_num(R1_num[1:0]), .Clock(Clock), .R2_num(R2_num[1:0]), .Din(in_2), .Reg2_out(n4regs_4_reg2_out),
    .Reg1_out(n4regs_4_reg1_out), .W_num(Write_Reg_num[1:0]), .WE(demultiplexer_1_out3));
  Multiplexer #(.select(2), .width(32), .enable("false")) multiplexer_1 (
    .in0(n4regs_1_reg2_out), .in1(n4regs_2_reg2_out), .in2(n4regs_3_reg2_out), .in3(n4regs_4_reg2_out),
    .out(Reg2_out), .sel(R2_num[3:2]));
  Multiplexer #(.select(2), .width(32), .enable("false")) multiplexer_2 (
    .in0(n4regs_1_reg1_out), .in1(n4regs_2_reg1_out), .in2(n4regs_3_reg1_out), .in3(n4regs_4_reg1_out),
    .out(Reg1_out), .sel(R1_num[3:2]));

  // Other names for the same wires on the sheet: Din[31:0] = in_2; W_num[3:0] = Write_Reg_num; WE = Write_Enable
endmodule

module RegsFile32 (
  input  [4:0] R1_num,
  input  [4:0] R2_num,
  input  WE,
  input  [4:0] W_num,
  input  [31:0] Din,
  input  Clock,
  output [31:0] out_7,
  output [31:0] out_8
);

  wire demultiplexer_1_out0, demultiplexer_1_out1;
  wire [31:0] regsfile16_1_reg1_out, regsfile16_1_reg2_out, regsfilezero16_1_reg1_out,
       regsfilezero16_1_reg2_out;

  Demultiplexer #(.enable("false")) demultiplexer_1 (
    .out0(demultiplexer_1_out0), .out1(demultiplexer_1_out1), .in(WE), .sel(W_num[4]));
  RegsFileZero16 regsfilezero16_1 (
    .R1_num(R1_num[3:0]), .in_2(Din), .R2_num(R2_num[3:0]), .Write_Reg_num(W_num[3:0]),
    .Write_Enable(demultiplexer_1_out0), .Clock(Clock), .Reg2_out(regsfilezero16_1_reg2_out),
    .Reg1_out(regsfilezero16_1_reg1_out));
  RegsFile16 regsfile16_1 (
    .R1_num(R1_num[3:0]), .in_2(Din), .R2_num(R2_num[3:0]), .Write_Reg_num(W_num[3:0]),
    .Write_Enable(demultiplexer_1_out1), .Clock(Clock), .Reg2_out(regsfile16_1_reg2_out),
    .Reg1_out(regsfile16_1_reg1_out));
  Multiplexer #(.width(32), .enable("false")) multiplexer_1 (
    .in0(regsfilezero16_1_reg2_out), .in1(regsfile16_1_reg2_out), .out(out_8), .sel(R2_num[4]));
  Multiplexer #(.width(32), .enable("false")) multiplexer_2 (
    .in0(regsfilezero16_1_reg1_out), .in1(regsfile16_1_reg1_out), .out(out_7), .sel(R1_num[4]));
endmodule

module RegsFile (
  input  [31:0] Din,
  input  [4:0] W_num,
  input  WE,
  input  [4:0] R1_num,
  input  [4:0] R2_num,
  input  Clock,
  output [31:0] v0,
  output [31:0] a0,
  output [31:0] a1,
  output [31:0] RD1,
  output [31:0] RD2
);

  wire demultiplexer_1_out0, demultiplexer_1_out1, demultiplexer_1_out2, demultiplexer_1_out3,
       demultiplexer_1_out4, demultiplexer_1_out5, demultiplexer_1_out6, demultiplexer_1_out7,
       demultiplexer_1_out8, demultiplexer_1_out9, demultiplexer_1_out10, demultiplexer_1_out11,
       demultiplexer_1_out12, demultiplexer_1_out13, demultiplexer_1_out14, demultiplexer_1_out15,
       demultiplexer_1_out16, demultiplexer_1_out17, demultiplexer_1_out18, demultiplexer_1_out19,
       demultiplexer_1_out20, demultiplexer_1_out21, demultiplexer_1_out22, demultiplexer_1_out23,
       demultiplexer_1_out24, demultiplexer_1_out25, demultiplexer_1_out26, demultiplexer_1_out27,
       demultiplexer_1_out28, demultiplexer_1_out29, demultiplexer_1_out30;
  wire [4:0] not_1_out;
  wire [31:0] a2_q, a3_q, at_q, fp_q, gp_q, k0_q, k1_q, ra_q, s0_q, s1_q, s2_q, s3_q, s4_q, s5_q, s6_q, s7_q,
       sp_q, t0_q, t1_q, t2_q, t3_q, t4_q, t5_q, t6_q, t7_q, t8_q, t9_q, v1_q;

  assign not_1_out = ~W_num;  // NOT_Gate not_1, 5 bits wide
  Demultiplexer #(.select(5), .enable("false")) demultiplexer_1 (
    .out0(demultiplexer_1_out0), .out1(demultiplexer_1_out1), .out2(demultiplexer_1_out2),
    .out3(demultiplexer_1_out3), .out4(demultiplexer_1_out4), .out5(demultiplexer_1_out5),
    .out6(demultiplexer_1_out6), .out7(demultiplexer_1_out7), .out8(demultiplexer_1_out8),
    .out9(demultiplexer_1_out9), .out10(demultiplexer_1_out10), .out11(demultiplexer_1_out11),
    .out12(demultiplexer_1_out12), .out13(demultiplexer_1_out13), .out14(demultiplexer_1_out14),
    .out15(demultiplexer_1_out15), .out16(demultiplexer_1_out16), .out17(demultiplexer_1_out17),
    .out18(demultiplexer_1_out18), .out19(demultiplexer_1_out19), .out20(demultiplexer_1_out20),
    .out21(demultiplexer_1_out21), .out22(demultiplexer_1_out22), .out23(demultiplexer_1_out23),
    .out24(demultiplexer_1_out24), .out25(demultiplexer_1_out25), .out26(demultiplexer_1_out26),
    .out27(demultiplexer_1_out27), .out28(demultiplexer_1_out28), .out29(demultiplexer_1_out29),
    .out30(demultiplexer_1_out30), .in(WE), .sel(not_1_out));  // open: out31
  Register #(.width(32), .Select("low")) t0 (.D(Din), .en(demultiplexer_1_out23), .Q(t0_q), .clk(Clock));  // open: clr
  Register #(.width(32), .Select("low")) s0 (.D(Din), .en(demultiplexer_1_out15), .Q(s0_q), .clk(Clock));  // open: clr
  Register #(.width(32), .Select("low")) t8 (.D(Din), .en(demultiplexer_1_out7), .Q(t8_q));  // open: clk, clr
  Register #(.width(32), .Select("low")) at (.D(Din), .en(demultiplexer_1_out30), .Q(at_q), .clk(Clock));  // open: clr
  Register #(.width(32), .Select("low")) t1 (.D(Din), .en(demultiplexer_1_out22), .Q(t1_q), .clk(Clock));  // open: clr
  Register #(.width(32), .Select("low")) s1 (.D(Din), .en(demultiplexer_1_out14), .Q(s1_q), .clk(Clock));  // open: clr
  Register #(.width(32), .Select("low")) t9 (.D(Din), .en(demultiplexer_1_out6), .Q(t9_q), .clk(Clock));  // open: clr
  Register #(.width(32), .Select("low")) u_v0 (.D(Din), .en(demultiplexer_1_out29), .Q(v0), .clk(Clock));  // open: clr
  Register #(.width(32), .Select("low")) t2 (.D(Din), .en(demultiplexer_1_out21), .Q(t2_q), .clk(Clock));  // open: clr
  Register #(.width(32), .Select("low")) s2 (.D(Din), .en(demultiplexer_1_out13), .Q(s2_q), .clk(Clock));  // open: clr
  Register #(.width(32), .Select("low")) k0 (.D(Din), .en(demultiplexer_1_out5), .Q(k0_q), .clk(Clock));  // open: clr
  Register #(.width(32), .Select("low")) v1 (.D(Din), .en(demultiplexer_1_out28), .Q(v1_q), .clk(Clock));  // open: clr
  Register #(.width(32), .Select("low")) t3 (.D(Din), .en(demultiplexer_1_out20), .Q(t3_q), .clk(Clock));  // open: clr
  Register #(.width(32), .Select("low")) s3 (.D(Din), .en(demultiplexer_1_out12), .Q(s3_q), .clk(Clock));  // open: clr
  Register #(.width(32), .Select("low")) k1 (.D(Din), .en(demultiplexer_1_out4), .Q(k1_q), .clk(Clock));  // open: clr
  Register #(.width(32), .Select("low")) u_a0 (.D(Din), .en(demultiplexer_1_out27), .Q(a0), .clk(Clock));  // open: clr
  Register #(.width(32), .Select("low")) t4 (.D(Din), .en(demultiplexer_1_out19), .Q(t4_q), .clk(Clock));  // open: clr
  Register #(.width(32), .Select("low")) s4 (.D(Din), .en(demultiplexer_1_out11), .Q(s4_q), .clk(Clock));  // open: clr
  Register #(.width(32), .Select("low")) gp (.D(Din), .en(demultiplexer_1_out3), .Q(gp_q), .clk(Clock));  // open: clr
  Register #(.width(32), .Select("low")) u_a1 (.D(Din), .en(demultiplexer_1_out26), .Q(a1), .clk(Clock));  // open: clr
  Register #(.width(32), .Select("low")) t5 (.D(Din), .en(demultiplexer_1_out18), .Q(t5_q), .clk(Clock));  // open: clr
  Register #(.width(32), .Select("low")) s5 (.D(Din), .en(demultiplexer_1_out10), .Q(s5_q), .clk(Clock));  // open: clr
  Register #(.width(32), .Select("low")) sp (.D(Din), .en(demultiplexer_1_out2), .Q(sp_q), .clk(Clock));  // open: clr
  Register #(.width(32), .Select("low")) a2 (.D(Din), .en(demultiplexer_1_out25), .Q(a2_q), .clk(Clock));  // open: clr
  Register #(.width(32), .Select("low")) t6 (.D(Din), .en(demultiplexer_1_out17), .Q(t6_q), .clk(Clock));  // open: clr
  Register #(.width(32), .Select("low")) s6 (.D(Din), .en(demultiplexer_1_out9), .Q(s6_q), .clk(Clock));  // open: clr
  Register #(.width(32), .Select("low")) fp (.D(Din), .en(demultiplexer_1_out1), .Q(fp_q), .clk(Clock));  // open: clr
  Register #(.width(32), .Select("low")) a3 (.D(Din), .en(demultiplexer_1_out24), .Q(a3_q), .clk(Clock));  // open: clr
  Register #(.width(32), .Select("low")) t7 (.D(Din), .en(demultiplexer_1_out16), .Q(t7_q), .clk(Clock));  // open: clr
  Register #(.width(32), .Select("low")) s7 (.D(Din), .en(demultiplexer_1_out8), .Q(s7_q), .clk(Clock));  // open: clr
  Register #(.width(32), .Select("low")) ra (.D(Din), .en(demultiplexer_1_out0), .Q(ra_q), .clk(Clock));  // open: clr
  Multiplexer #(.select(5), .width(32), .enable("false")) multiplexer_1 (
    .in0({32{1'b0}}), .in1(at_q), .in2(v0), .in3(v1_q), .in4(a0), .in5(a1), .in6(a2_q), .in7(a3_q),
    .in8(t0_q), .in9(t1_q), .in10(t2_q), .in11(t3_q), .in12(t4_q), .in13(t5_q), .in14(t6_q), .in15(t7_q),
    .in16(s0_q), .in17(s1_q), .in18(s2_q), .in19(s3_q), .in20(s4_q), .in21(s5_q), .in22(s6_q), .in23(s7_q),
    .in24(t8_q), .in25(t9_q), .in26(k0_q), .in27(k1_q), .in28(gp_q), .in29(sp_q), .in30(fp_q), .in31(ra_q),
    .out(RD1), .sel(R1_num));
  Multiplexer #(.select(5), .width(32), .enable("false")) multiplexer_2 (
    .in0({32{1'b0}}), .in1(at_q), .in2(v0), .in3(v1_q), .in4(a0), .in5(a1), .in6(a2_q), .in7(a3_q),
    .in8(t0_q), .in9(t1_q), .in10(t2_q), .in11(t3_q), .in12(t4_q), .in13(t5_q), .in14(t6_q), .in15(t7_q),
    .in16(s0_q), .in17(s1_q), .in18(s2_q), .in19(s3_q), .in20(s4_q), .in21(s5_q), .in22(s6_q), .in23(s7_q),
    .in24(t8_q), .in25(t9_q), .in26(k0_q), .in27(k1_q), .in28(gp_q), .in29(sp_q), .in30(fp_q), .in31(ra_q),
    .out(RD2), .sel(R2_num));
endmodule
